// Logisim project sqrt2.circ as structural Verilog: 30 circuits, main circuit sqrt
module main (
  input  ENABLE,
  input  [15:0] IO_DATA_IN,
  output NAN,
  output PINF,
  output NINF,
  output RESULT,
  output [15:0] IO_DATA_OUT
);

  wire CLK_out;

  Clock CLK (.out(CLK_out));
  sqrt sqrt_1 (
    .CLK(CLK_out), .ENABLE(ENABLE), .IO_DATA_IN(IO_DATA_IN), .IS_NAN(NAN), .IS_PINF(PINF), .IS_NINF(NINF),
    .RESULT(RESULT), .IO_DATA_OUT(IO_DATA_OUT));
endmodule

module sqrt (
  input  CLK,
  input  ENABLE,
  input  [15:0] IO_DATA_IN,
  output IS_NAN,
  output IS_PINF,
  output IS_NINF,
  output RESULT,
  output [15:0] IO_DATA_OUT
);

  wire and_1_out, ENABLE_t, if_tick_eq_x_1_ans, if_tick_more_x_1_ans, not_1_out, or_1_out, SIGN,
       transmission_1_p2, transmission_2_p2;
  wire [5:0] CUR_TICK;
  wire [14:0] dtrigger16_1_q;
  wire [15:0] transmission_1_p1;
  wire [31:0] EXP, MANT;

  not not_1 (not_1_out, ENABLE_t);
  or or_1 (or_1_out, 1'b0, not_1_out);
  D_WithoutEnabled d_withoutenabled_1 (.D(ENABLE), .C(CLK), .Q(ENABLE_t));  // open: NQ
  // Probe on CUR_TICK
  Counter counter_1 (.Enabled(ENABLE_t), .CLK(CLK), .Done(or_1_out), .CUR_TICK(CUR_TICK));
  // Probe on transmission_1_p1
  and and_1 (and_1_out, CLK, transmission_1_p2);
  IF_Tick_eq_x if_tick_eq_x_1 (.Tick(CUR_TICK), .X({8{1'b0}}), .ans(if_tick_eq_x_1_ans));
  // NOT_Gate not_2 has open pins: in=transmission_1_p2, out=open
  // Transmission_Gate #(.width(16)) transmission_1: pin names not known; wires that end beside it: transmission_1_p1, transmission_1_p2, IO_DATA_IN
  DTrigger16 dtrigger16_1 (
    .D(transmission_1_p1), .C(and_1_out), .Enabled(ENABLE_t), .Q({SIGN, dtrigger16_1_q}));  // open: NQ
  and and_2 (transmission_1_p2, if_tick_eq_x_1_ans, ENABLE_t);
  // Probe on {SIGN, dtrigger16_1_q}
  IF_Tick_more_x if_tick_more_x_1 (.Tick(CUR_TICK), .X(8'h1), .ans(if_tick_more_x_1_ans));
  // Transmission_Gate #(.width(16)) transmission_2: pin names not known; wires that end beside it: IO_DATA_IN, transmission_2_p2, {16{1'b1}}
  and and_3 (transmission_2_p2, if_tick_more_x_1_ans, ENABLE_t);
  // NOT_Gate not_3 has open pins: in=transmission_2_p2, out=open
  assign MANT = {{22{dtrigger16_1_q[9]}}, dtrigger16_1_q[9:0]};  // Bit_Extender bit_extender_1
  assign EXP = {{27{dtrigger16_1_q[14]}}, dtrigger16_1_q[14:10]};  // Bit_Extender bit_extender_2

  assign IO_DATA_OUT = IO_DATA_IN;
  assign RESULT = 1'b0;
endmodule

module RS (
  input  R,
  input  C,
  input  S,
  output Q,
  output NQ
);

  wire nand_1_out, nand_2_out, nand_4_out, por_1_out;

  nand nand_1 (nand_1_out, S, C);
  nand nand_2 (nand_2_out, C, R);
  POR por_1 (.out(por_1_out));
  nand nand_3 (Q, nand_1_out, NQ);
  nand nand_4 (nand_4_out, Q, nand_2_out);
  or or_1 (NQ, nand_4_out, por_1_out);
endmodule

module Dtrigger1 (
  input  D,
  input  C,
  input  Enabled,
  output Q,
  output NQ
);

  wire not_1_out;

  not not_1 (not_1_out, D);
  JK jk_1 (.K(not_1_out), .C(C), .J(D), .Enabled(Enabled), .Q(Q), .NQ(NQ));
endmodule

module DTrigger2 (
  input  [1:0] D,
  input  C,
  input  Enabled,
  output [1:0] Q,
  output [1:0] NQ
);

  Dtrigger1 dtrigger1_1 (.D(D[0]), .C(C), .Enabled(Enabled), .Q(Q[0]), .NQ(NQ[0]));
  Dtrigger1 dtrigger1_2 (.D(D[1]), .C(C), .Enabled(Enabled), .Q(Q[1]), .NQ(NQ[1]));
endmodule

module DTrigger4 (
  input  [3:0] D,
  input  C,
  input  Enabled,
  output [3:0] Q,
  output [3:0] NQ
);

  DTrigger2 dtrigger2_1 (.D(D[1:0]), .C(C), .Enabled(Enabled), .Q(Q[1:0]), .NQ(NQ[1:0]));
  DTrigger2 dtrigger2_2 (.D(D[3:2]), .C(C), .Enabled(Enabled), .Q(Q[3:2]), .NQ(NQ[3:2]));
endmodule

module DTrigger8 (
  input  [7:0] D,
  input  C,
  input  Enabled,
  output [7:0] Q,
  output [7:0] NQ
);

  DTrigger4 dtrigger4_1 (.D(D[3:0]), .C(C), .Enabled(Enabled), .Q(Q[3:0]), .NQ(NQ[3:0]));
  DTrigger4 dtrigger4_2 (.D(D[7:4]), .C(C), .Enabled(Enabled), .Q(Q[7:4]), .NQ(NQ[7:4]));
endmodule

module DTrigger16 (
  input  [15:0] D,
  input  C,
  input  Enabled,
  output [15:0] Q,
  output [15:0] NQ
);

  DTrigger8 dtrigger8_1 (.D(D[7:0]), .C(C), .Enabled(Enabled), .Q(Q[7:0]), .NQ(NQ[7:0]));
  DTrigger8 dtrigger8_2 (.D(D[15:8]), .C(C), .Enabled(Enabled), .Q(Q[15:8]), .NQ(NQ[15:8]));
endmodule

module DTrigger32 (
  input  [31:0] D,
  input  C,
  input  Enabled,
  output [31:0] Q,
  output [31:0] NQ
);

  DTrigger16 dtrigger16_1 (.D(D[15:0]), .C(C), .Enabled(Enabled), .Q(Q[15:0]), .NQ(NQ[15:0]));
  DTrigger16 dtrigger16_2 (.D(D[31:16]), .C(C), .Enabled(Enabled), .Q(Q[31:16]), .NQ(NQ[31:16]));
endmodule

module SUM1 (
  input  A,
  input  B,
  input  Cin,
  output S,
  output Cout
);

  wire and_1_out, and_2_out, xor_1_out;

  xor xor_1 (xor_1_out, A, B);
  xor xor_2 (S, xor_1_out, Cin);
  and and_1 (and_1_out, xor_1_out, Cin);
  and and_2 (and_2_out, A, B);
  or or_1 (Cout, and_1_out, and_2_out);
endmodule

module SUM2 (
  input  [1:0] A,
  input  [1:0] B,
  input  Cin,
  output [1:0] S,
  output Cout
);

  wire sum1_1_cout;

  SUM1 sum1_1 (.A(A[0]), .B(B[0]), .Cin(Cin), .S(S[0]), .Cout(sum1_1_cout));
  SUM1 sum1_2 (.A(A[1]), .B(B[1]), .Cin(sum1_1_cout), .S(S[1]), .Cout(Cout));
endmodule

module SUM4 (
  input  [3:0] A,
  input  [3:0] B,
  input  Cin,
  output [3:0] S,
  output Cout
);

  wire sum2_1_cout;

  SUM2 sum2_1 (.A(A[1:0]), .B(B[1:0]), .Cin(Cin), .S(S[1:0]), .Cout(sum2_1_cout));
  SUM2 sum2_2 (.A(A[3:2]), .B(B[3:2]), .Cin(sum2_1_cout), .S(S[3:2]), .Cout(Cout));
endmodule

module SUM8 (
  input  [7:0] A,
  input  [7:0] B,
  input  Cin,
  output [7:0] S,
  output Cout
);

  wire sum4_1_cout;

  SUM4 sum4_1 (.A(A[3:0]), .B(B[3:0]), .Cin(Cin), .S(S[3:0]), .Cout(sum4_1_cout));
  SUM4 sum4_2 (.A(A[7:4]), .B(B[7:4]), .Cin(sum4_1_cout), .S(S[7:4]), .Cout(Cout));
endmodule

module SUM16 (
  input  [15:0] A,
  input  [15:0] B,
  input  Cin,
  output [15:0] S,
  output Cout
);

  wire sum8_1_cout;

  SUM8 sum8_1 (.A(A[7:0]), .B(B[7:0]), .Cin(Cin), .S(S[7:0]), .Cout(sum8_1_cout));
  SUM8 sum8_2 (.A(A[15:8]), .B(B[15:8]), .Cin(sum8_1_cout), .S(S[15:8]), .Cout(Cout));
endmodule

module SUM32 (
  input  [31:0] A,
  input  [31:0] B,
  input  Cin,
  output [31:0] S,
  output Cout
);

  wire sum16_1_cout;

  SUM16 sum16_1 (.A(A[15:0]), .B(B[15:0]), .Cin(Cin), .S(S[15:0]), .Cout(sum16_1_cout));
  SUM16 sum16_2 (.A(A[31:16]), .B(B[31:16]), .Cin(sum16_1_cout), .S(S[31:16]), .Cout(Cout));
endmodule

module Counter (
  input  Enabled,
  input  CLK,
  input  Done,
  output [5:0] CUR_TICK
);

  wire and_1_out, not_1_out;

  and and_1 (and_1_out, CLK, not_1_out);
  not not_1 (not_1_out, Done);
  T t_1 (.CLK(and_1_out), .Enabled(Enabled), .Tick(CUR_TICK[0]));
  T t_2 (.CLK(CUR_TICK[0]), .Enabled(Enabled), .Tick(CUR_TICK[1]));
  T t_3 (.CLK(CUR_TICK[1]), .Enabled(Enabled), .Tick(CUR_TICK[2]));
  T t_4 (.CLK(CUR_TICK[2]), .Enabled(Enabled), .Tick(CUR_TICK[3]));
  T t_5 (.CLK(CUR_TICK[3]), .Enabled(Enabled), .Tick(CUR_TICK[4]));
  T t_6 (.CLK(CUR_TICK[4]), .Enabled(Enabled), .Tick(CUR_TICK[5]));
endmodule

module T (
  input  CLK,
  input  Enabled,
  output Tick
);

  wire dtrigger1_1_nq;

  Dtrigger1 dtrigger1_1 (.D(dtrigger1_1_nq), .C(CLK), .Enabled(Enabled), .Q(Tick), .NQ(dtrigger1_1_nq));
endmodule

module MINUS32 (
  input  [31:0] A,
  input  [31:0] B,
  output [31:0] S,
  output Cout
);

  wire [31:0] sum32_1_s, xor_1_out;

  assign xor_1_out = {32{1'b1}} ^ B;  // XOR_Gate xor_1, 32 bits wide
  // Probe on xor_1_out
  SUM32 sum32_1 (.A(32'h1), .B(xor_1_out), .S(sum32_1_s));  // open: Cin, Cout
  // Probe on sum32_1_s
  SUM32 sum32_2 (.A(A), .B(sum32_1_s), .S(S), .Cout(Cout));  // open: Cin
endmodule

module COMP1 (
  input  A,
  input  B,
  output EQ,
  output MORE,
  output LESS
);

  wire not_1_out, not_2_out, not_3_out, not_4_out;

  xnor xnor_1 (EQ, A, B);
  not not_1 (not_1_out, EQ);
  not not_2 (not_2_out, B);
  not not_3 (not_3_out, EQ);
  not not_4 (not_4_out, A);
  and and_1 (MORE, not_1_out, not_2_out);
  and and_2 (LESS, not_3_out, not_4_out);
endmodule

module COMP2 (
  input  [1:0] A,
  input  [1:0] B,
  output EQ,
  output MORE,
  output LESS
);

  wire and_2_out, and_3_out, comp1_1_eq, comp1_1_less, comp1_1_more, comp1_2_eq, comp1_2_less, comp1_2_more;

  COMP1 comp1_1 (.A(A[1]), .B(B[1]), .EQ(comp1_1_eq), .MORE(comp1_1_more), .LESS(comp1_1_less));
  COMP1 comp1_2 (.A(A[0]), .B(B[0]), .EQ(comp1_2_eq), .MORE(comp1_2_more), .LESS(comp1_2_less));
  and and_1 (EQ, comp1_1_eq, comp1_2_eq);
  and and_2 (and_2_out, comp1_1_eq, comp1_2_more);
  or or_1 (MORE, comp1_1_more, and_2_out);
  or or_2 (LESS, comp1_1_less, and_3_out);
  and and_3 (and_3_out, comp1_1_eq, comp1_2_less);
endmodule

module COMP4 (
  input  [3:0] A,
  input  [3:0] B,
  output EQ,
  output MORE,
  output LESS
);

  wire and_2_out, and_3_out, comp2_1_eq, comp2_1_less, comp2_1_more, comp2_2_eq, comp2_2_less, comp2_2_more;

  COMP2 comp2_1 (.A(A[3:2]), .B(B[3:2]), .EQ(comp2_1_eq), .MORE(comp2_1_more), .LESS(comp2_1_less));
  COMP2 comp2_2 (.A(A[1:0]), .B(B[1:0]), .EQ(comp2_2_eq), .MORE(comp2_2_more), .LESS(comp2_2_less));
  and and_1 (EQ, comp2_1_eq, comp2_2_eq);
  and and_2 (and_2_out, comp2_1_eq, comp2_2_more);
  or or_1 (MORE, comp2_1_more, and_2_out);
  or or_2 (LESS, comp2_1_less, and_3_out);
  and and_3 (and_3_out, comp2_1_eq, comp2_2_less);
endmodule

module COMP8 (
  input  [7:0] A,
  input  [7:0] B,
  output EQ,
  output MORE,
  output LESS
);

  wire and_2_out, and_3_out, comp4_1_eq, comp4_1_less, comp4_1_more, comp4_2_eq, comp4_2_less, comp4_2_more;

  COMP4 comp4_1 (.A(A[7:4]), .B(B[7:4]), .EQ(comp4_1_eq), .MORE(comp4_1_more), .LESS(comp4_1_less));
  COMP4 comp4_2 (.A(A[3:0]), .B(B[3:0]), .EQ(comp4_2_eq), .MORE(comp4_2_more), .LESS(comp4_2_less));
  and and_1 (EQ, comp4_1_eq, comp4_2_eq);
  and and_2 (and_2_out, comp4_1_eq, comp4_2_more);
  or or_1 (MORE, comp4_1_more, and_2_out);
  or or_2 (LESS, comp4_1_less, and_3_out);
  and and_3 (and_3_out, comp4_1_eq, comp4_2_less);
endmodule

module COMP16 (
  input  [15:0] A,
  input  [15:0] B,
  output EQ,
  output MORE,
  output LESS
);

  wire and_2_out, and_3_out, comp8_1_eq, comp8_1_less, comp8_1_more, comp8_2_eq, comp8_2_less, comp8_2_more;

  COMP8 comp8_1 (.A(A[15:8]), .B(B[15:8]), .EQ(comp8_1_eq), .MORE(comp8_1_more), .LESS(comp8_1_less));
  COMP8 comp8_2 (.A(A[7:0]), .B(B[7:0]), .EQ(comp8_2_eq), .MORE(comp8_2_more), .LESS(comp8_2_less));
  and and_1 (EQ, comp8_1_eq, comp8_2_eq);
  and and_2 (and_2_out, comp8_1_eq, comp8_2_more);
  or or_1 (MORE, comp8_1_more, and_2_out);
  or or_2 (LESS, comp8_1_less, and_3_out);
  and and_3 (and_3_out, comp8_1_eq, comp8_2_less);
endmodule

module COMP32 (
  input  [31:0] A,
  input  [31:0] B,
  output EQ,
  output MORE,
  output LESS
);

  wire and_2_out, and_3_out, comp16_1_eq, comp16_1_less, comp16_1_more, comp16_2_eq, comp16_2_less,
       comp16_2_more;

  COMP16 comp16_1 (.A(A[31:16]), .B(B[31:16]), .EQ(comp16_1_eq), .MORE(comp16_1_more), .LESS(comp16_1_less));
  COMP16 comp16_2 (.A(A[15:0]), .B(B[15:0]), .EQ(comp16_2_eq), .MORE(comp16_2_more), .LESS(comp16_2_less));
  and and_1 (EQ, comp16_1_eq, comp16_2_eq);
  and and_2 (and_2_out, comp16_1_eq, comp16_2_more);
  or or_1 (MORE, comp16_1_more, and_2_out);
  or or_2 (LESS, comp16_1_less, and_3_out);
  and and_3 (and_3_out, comp16_1_eq, comp16_2_less);
endmodule

module RS_WITH_ENABLED (
  input  R,
  input  C,
  input  S,
  input  Enabled,
  output Q,
  output NQ
);

  wire and_1_out, nand_1_out, nand_2_out, nand_3_out, nand_4_out, or_1_out, por_1_out;

  nand nand_1 (nand_1_out, S, C);
  nand nand_2 (nand_2_out, C, R);
  POR por_1 (.out(por_1_out));
  nand nand_3 (nand_3_out, nand_1_out, or_1_out);
  nand nand_4 (nand_4_out, and_1_out, nand_2_out);
  and and_1 (and_1_out, Enabled, nand_3_out);
  or or_1 (or_1_out, nand_4_out, por_1_out);
  and and_2 (Q, Enabled, and_1_out);
  not not_1 (NQ, Q);
endmodule

module JK (
  input  K,
  input  C,
  input  J,
  input  Enabled,
  output Q,
  output NQ
);

  wire and_1_out, and_2_out, not_1_out, rs_with_enabled_1_nq, rs_with_enabled_1_q;

  and and_1 (and_1_out, Q, K);
  and and_2 (and_2_out, J, NQ);
  RS_WITH_ENABLED rs_with_enabled_1 (
    .R(and_1_out), .C(C), .S(and_2_out), .Enabled(Enabled), .Q(rs_with_enabled_1_q), .NQ(rs_with_enabled_1_nq));
  not not_1 (not_1_out, C);
  RS rs_1 (.R(rs_with_enabled_1_nq), .C(not_1_out), .S(rs_with_enabled_1_q), .Q(Q), .NQ(NQ));
endmodule

module D_WithoutEnabled (
  input  D,
  input  C,
  output Q,
  output NQ
);

  Dtrigger1 dtrigger1_1 (.D(D), .C(C), .Enabled(1'b1), .Q(Q), .NQ(NQ));
endmodule

module IF_Tick_eq_x (
  input  [5:0] Tick,
  input  [7:0] X,
  output ans
);

  wire [7:0] bit_extender_1_out;

  assign bit_extender_1_out = {{2{1'b0}}, Tick};  // Bit_Extender bit_extender_1
  // Probe on bit_extender_1_out
  COMP8 comp8_1 (.A(bit_extender_1_out), .B(X), .EQ(ans));  // open: MORE, LESS
endmodule

module IF_Tick_more_x (
  input  [5:0] Tick,
  input  [7:0] X,
  output ans
);

  wire comp8_1_eq;
  wire [7:0] bit_extender_1_out;

  assign bit_extender_1_out = {{2{1'b0}}, Tick};  // Bit_Extender bit_extender_1
  // Probe on bit_extender_1_out
  COMP8 comp8_1 (.A(bit_extender_1_out), .B(X), .EQ(comp8_1_eq), .MORE(ans));  // open: LESS
endmodule

module IF_Tick_less_x (
  input  [5:0] Tick,
  input  [7:0] X,
  output ans
);

  wire comp8_1_eq;
  wire [7:0] bit_extender_1_out;

  assign bit_extender_1_out = {{2{1'b0}}, Tick};  // Bit_Extender bit_extender_1
  // Probe on bit_extender_1_out
  COMP8 comp8_1 (.A(bit_extender_1_out), .B(X), .EQ(comp8_1_eq), .LESS(ans));  // open: MORE
endmodule
